// Digital circuit ALU_completa_t_Com1_Grupo01.dig as structural Verilog
module ALU_completa_t_Com1_Grupo01 (
  input  [3:0] nro1,
  input  [3:0] nro2,
  input  [1:0] selec,
  output [3:0] resul,
  output [3:0] flags
);

  wire notconnected_1_out;
  wire [3:0] and_1_out, and_2_out, and_3_out, and_4_out, funclog_nbits_1_r, sumarit_nbits_1_r,
       sumarit_nbits_1_zcvn;
  wire [3:3] nor_1_out, not_1_out;

  not not_1 (not_1_out[3], selec[1]);
  SumArit_Nbits sumarit_nbits_1 (.A(nro1), .B(nro2), .OP(selec[0]), .R(sumarit_nbits_1_r), .zcvn(sumarit_nbits_1_zcvn));
  FuncLog_Nbits funclog_nbits_1 (.A(nro1), .B(nro2), .OP(selec[0]), .R(funclog_nbits_1_r));
  assign and_1_out = funclog_nbits_1_r & {4{selec[1]}};  // And and_1, 4 bits wide
  assign and_2_out = {4{not_1_out[3]}} & sumarit_nbits_1_r;  // And and_2, 4 bits wide
  assign and_3_out = sumarit_nbits_1_zcvn & {4{not_1_out[3]}};  // And and_3, 4 bits wide
  assign resul = and_1_out ^ and_2_out;  // XOr xor_1, 4 bits wide
  nor nor_1 (nor_1_out[3], and_1_out[0], and_1_out[1], and_1_out[2], and_1_out[3]);
  assign and_4_out = {nor_1_out[3], 2'b00, and_1_out[3]} & {4{selec[1]}};  // And and_4, 4 bits wide
  Seven_Seg_Hex seven_seg_hex_1 (.d(resul), .dp(notconnected_1_out));
  // NotConnected on notconnected_1_out
  assign flags = and_3_out ^ and_4_out;  // XOr xor_2, 4 bits wide
endmodule
