// Digital circuit FuncLog_Nbits.dig as structural Verilog
module FuncLog_Nbits (
  input  [7:0] A,
  input  [7:0] B,
  input  OP,
  output [7:0] R
);

  wire [7:0] and_1_out, and_2_out, and_3_out, not_1_out, or_1_out;

  assign or_1_out = A | B;  // Or or_1, 8 bits wide
  assign and_1_out = B & A;  // And and_1, 8 bits wide
  assign not_1_out = ~{8{OP}};  // Not not_1, 8 bits wide
  assign and_2_out = or_1_out & {8{OP}};  // And and_2, 8 bits wide
  assign and_3_out = and_1_out & not_1_out;  // And and_3, 8 bits wide
  assign R = and_2_out ^ and_3_out;  // XOr xor_1, 8 bits wide
endmodule
