// Digital circuit SumArit_Nbits.dig as structural Verilog
module SumArit_Nbits (
  input  [7:0] A,
  input  [7:0] B,
  input  OP,
  output [7:0] R,
  output [3:0] zcvn
);

  wire and_1_out, and_2_out, not_1_out, not_2_out, sum_4bit_t_com1_grupo01_1_cout;
  wire [7:0] complementadora2_t_com1_grupo01_1_b;

  complementadorA2_t_Com1_Grupo01 complementadora2_t_com1_grupo01_1 (
    .B_2(B), .Neg(OP), .B(complementadora2_t_com1_grupo01_1_b));
  sum_4bit_t_Com1_Grupo01 sum_4bit_t_com1_grupo01_1 (
    .A(A), .B(complementadora2_t_com1_grupo01_1_b), .Cin(1'b0), .S(R), .Cout(sum_4bit_t_com1_grupo01_1_cout));
  and and_1 (and_1_out, not_1_out, OP);
  not not_1 (not_1_out, sum_4bit_t_com1_grupo01_1_cout);
  not not_2 (not_2_out, OP);
  flag_overflow_t_Com1_Grupo01 flag_overflow_t_com1_grupo01_1 (
    .a3(A[7]), .b3(complementadora2_t_com1_grupo01_1_b[7]), .s3(R[7]), .V(zcvn[1]));
  and and_2 (and_2_out, sum_4bit_t_com1_grupo01_1_cout, not_2_out);
  flag_cero_t_Com1_Grupo01 flag_cero_t_com1_grupo01_1 (.S(R), .Z(zcvn[3]));
  xor xor_1 (zcvn[2], and_1_out, and_2_out);

  assign zcvn[0] = R[7];
endmodule
