// Digital circuit complementadorA2_t_Com1_Grupo01.dig as structural Verilog
module complementadorA2_t_Com1_Grupo01 (
  input  [3:0] B_2,
  input  Neg,
  output [3:0] B
);

  wire notconnected_1_out;
  wire [3:0] xor_1_out;

  assign xor_1_out = B_2 ^ {4{Neg}};  // XOr xor_1, 4 bits wide
  sum_4bit_t_Com1_Grupo01 sum_4bit_t_com1_grupo01_1 (.A(xor_1_out), .B(4'b0000), .Cin(Neg), .S(B));  // open: Cout
  Seven_Seg_Hex seven_seg_hex_1 (.d(B), .dp(notconnected_1_out));
  // NotConnected on notconnected_1_out
endmodule
