// Digital circuit sum_4bit_t_Com1_Grupo01.dig as structural Verilog
module sum_4bit_t_Com1_Grupo01 (
  input  [3:0] A,
  input  [3:0] B,
  input  Cin,
  output [3:0] S,
  output Cout
);

  wire sum_1bit_t_com1_grupo01_1_cout, sum_1bit_t_com1_grupo01_2_cout, sum_1bit_t_com1_grupo01_3_cout;

  sum_1bit_t_Com1_Grupo01 sum_1bit_t_com1_grupo01_1 (
    .A(A[0]), .B(B[0]), .Cin(Cin), .S(S[0]), .Cout(sum_1bit_t_com1_grupo01_1_cout));
  sum_1bit_t_Com1_Grupo01 sum_1bit_t_com1_grupo01_2 (
    .A(A[1]), .B(B[1]), .Cin(sum_1bit_t_com1_grupo01_1_cout), .S(S[1]), .Cout(sum_1bit_t_com1_grupo01_2_cout));
  sum_1bit_t_Com1_Grupo01 sum_1bit_t_com1_grupo01_3 (
    .A(A[2]), .B(B[2]), .Cin(sum_1bit_t_com1_grupo01_2_cout), .S(S[2]), .Cout(sum_1bit_t_com1_grupo01_3_cout));
  sum_1bit_t_Com1_Grupo01 sum_1bit_t_com1_grupo01_4 (
    .A(A[3]), .B(B[3]), .Cin(sum_1bit_t_com1_grupo01_3_cout), .S(S[3]), .Cout(Cout));
  Seven_Seg_Hex seven_seg_hex_1 (.d(S), .dp(Cout));
endmodule
